// Logisim project renamed.circ as structural Verilog: 2 circuits, main circuit main
module main (
  input  [4:0] a1,
  output [31:0] out_2
);

  wire [31:0] o_00, o_01, o_02, o_03, o_04, o_05, o_06, o_07, o_08, o_09, o_10, o_11, o_12, o_13, o_14, o_15,
       o_16, o_17, o_18, o_19, o_20, o_21, o_22, o_23, o_24, o_25, o_26, o_27, o_28, o_29, o_30, o_31;

  Multiplexer #(.select(5), .width(32), .enable("false")) multiplexer_1 (
    .in0(o_00), .in1(o_01), .in2(o_02), .in3(o_03), .in4(o_04), .in5(o_05), .in6(o_06), .in7(o_07),
    .in8(o_08), .in9(o_09), .in10(o_10), .in11(o_11), .in12(o_12), .in13(o_13), .in14(o_14), .in15(o_15),
    .in16(o_16), .in17(o_17), .in18(o_18), .in19(o_19), .in20(o_20), .in21(o_21), .in22(o_22), .in23(o_23),
    .in24(o_24), .in25(o_25), .in26(o_26), .in27(o_27), .in28(o_28), .in29(o_29), .in30(o_30), .in31(o_31),
    .out(out_2), .sel(a1));
endmodule

module regs (
);

  wire clk, clr, en;
  wire [31:0] i_00, i_01, i_02, i_03, i_04, i_05, i_06, i_07, i_08, i_09, i_10, i_11, i_12, i_13, i_14, i_15,
       i_16, i_17, i_18, i_19, i_20, i_21, i_22, i_23, i_24, i_25, i_26, i_27, i_28, i_29, i_30, i_31, o_00,
       o_01, o_02, o_03, o_04, o_05, o_06, o_07, o_08, o_09, o_10, o_11, o_12, o_13, o_14, o_15, o_16, o_17,
       o_18, o_19, o_20, o_21, o_22, o_23, o_24, o_25, o_26, o_27, o_28, o_29, o_30, o_31;

  Register #(.width(32)) register_1 (.D(i_00), .en(en), .Q(o_00), .clk(clk), .clr(clr));
  Register #(.width(32)) register_2 (.D(i_08), .en(en), .Q(o_08), .clk(clk), .clr(clr));
  Register #(.width(32)) register_3 (.D(i_16), .en(en), .Q(o_16), .clk(clk), .clr(clr));
  Register #(.width(32)) register_4 (.D(i_24), .en(en), .Q(o_24), .clk(clk), .clr(clr));
  Register #(.width(32)) register_5 (.D(i_01), .en(en), .Q(o_01), .clk(clk), .clr(clr));
  Register #(.width(32)) register_6 (.D(i_09), .en(en), .Q(o_09), .clk(clk), .clr(clr));
  Register #(.width(32)) register_7 (.D(i_17), .en(en), .Q(o_17), .clk(clk), .clr(clr));
  Register #(.width(32)) register_8 (.D(i_25), .en(en), .Q(o_25), .clk(clk), .clr(clr));
  Register #(.width(32)) register_9 (.D(i_02), .en(en), .Q(o_02), .clk(clk), .clr(clr));
  Register #(.width(32)) register_10 (.D(i_10), .en(en), .Q(o_10), .clk(clk), .clr(clr));
  Register #(.width(32)) register_11 (.D(i_18), .en(en), .Q(o_18), .clk(clk), .clr(clr));
  Register #(.width(32)) register_12 (.D(i_26), .en(en), .Q(o_26), .clk(clk), .clr(clr));
  Register #(.width(32)) register_13 (.D(i_03), .en(en), .Q(o_03), .clk(clk), .clr(clr));
  Register #(.width(32)) register_14 (.D(i_11), .en(en), .Q(o_11), .clk(clk), .clr(clr));
  Register #(.width(32)) register_15 (.D(i_19), .en(en), .Q(o_19), .clk(clk), .clr(clr));
  Register #(.width(32)) register_16 (.D(i_27), .en(en), .Q(o_27), .clk(clk), .clr(clr));
  Register #(.width(32)) register_17 (.D(i_04), .en(en), .Q(o_04), .clk(clk), .clr(clr));
  Register #(.width(32)) register_18 (.D(i_12), .en(en), .Q(o_12), .clk(clk), .clr(clr));
  Register #(.width(32)) register_19 (.D(i_20), .en(en), .Q(o_20), .clk(clk), .clr(clr));
  Register #(.width(32)) register_20 (.D(i_28), .en(en), .Q(o_28), .clk(clk), .clr(clr));
  Register #(.width(32)) register_21 (.D(i_05), .en(en), .Q(o_05), .clk(clk), .clr(clr));
  Register #(.width(32)) register_22 (.D(i_13), .en(en), .Q(o_13), .clk(clk), .clr(clr));
  Register #(.width(32)) register_23 (.D(i_21), .en(en), .Q(o_21), .clk(clk), .clr(clr));
  Register #(.width(32)) register_24 (.D(i_29), .en(en), .Q(o_29), .clk(clk), .clr(clr));
  Register #(.width(32)) register_25 (.D(i_06), .en(en), .Q(o_06), .clk(clk), .clr(clr));
  Register #(.width(32)) register_26 (.D(i_14), .en(en), .Q(o_14), .clk(clk), .clr(clr));
  Register #(.width(32)) register_27 (.D(i_22), .en(en), .Q(o_22), .clk(clk), .clr(clr));
  Register #(.width(32)) register_28 (.D(i_30), .en(en), .Q(o_30), .clk(clk), .clr(clr));
  Register #(.width(32)) register_29 (.D(i_07), .en(en), .Q(o_07), .clk(clk), .clr(clr));
  Register #(.width(32)) register_30 (.D(i_15), .en(en), .Q(o_15), .clk(clk), .clr(clr));
  Register #(.width(32)) register_31 (.D(i_23), .en(en), .Q(o_23), .clk(clk), .clr(clr));
  Register #(.width(32)) register_32 (.D(i_31), .en(en), .Q(o_31), .clk(clk), .clr(clr));
endmodule
