// Logisim project sample.circ as structural Verilog: 2 circuits, main circuit main
module main (
  input  [4:0] a1,
  output [31:0] out_2
);

  wire [31:0] o_00;

  Multiplexer #(.select(5), .width(32), .enable("false")) multiplexer_1 (
    .in0(o_00), .in1(o_00), .in2(o_00), .in3(o_00), .in4(o_00), .in5(o_00), .in6(o_00), .in7(o_00),
    .in8(o_00), .in9(o_00), .in10(o_00), .in11(o_00), .in12(o_00), .in13(o_00), .in14(o_00), .in15(o_00),
    .in16(o_00), .in17(o_00), .in18(o_00), .in19(o_00), .in20(o_00), .in21(o_00), .in22(o_00), .in23(o_00),
    .in24(o_00), .in25(o_00), .in26(o_00), .in27(o_00), .in28(o_00), .in29(o_00), .in30(o_00), .in31(o_00),
    .out(out_2), .sel(a1));
endmodule

module regs (
);

  wire clk, clr, en;
  wire [31:0] i_00, o_00;

  Register #(.width(32)) register_1 (.D(i_00), .en(en), .Q(o_00), .clk(clk), .clr(clr));
  Register #(.width(32)) register_2 (.D(i_00), .en(en), .Q(o_00), .clk(clk), .clr(clr));
  Register #(.width(32)) register_3 (.D(i_00), .en(en), .Q(o_00), .clk(clk), .clr(clr));
  Register #(.width(32)) register_4 (.D(i_00), .en(en), .Q(o_00), .clk(clk), .clr(clr));
  Register #(.width(32)) register_5 (.D(i_00), .en(en), .Q(o_00), .clk(clk), .clr(clr));
  Register #(.width(32)) register_6 (.D(i_00), .en(en), .Q(o_00), .clk(clk), .clr(clr));
  Register #(.width(32)) register_7 (.D(i_00), .en(en), .Q(o_00), .clk(clk), .clr(clr));
  Register #(.width(32)) register_8 (.D(i_00), .en(en), .Q(o_00), .clk(clk), .clr(clr));
  Register #(.width(32)) register_9 (.D(i_00), .en(en), .Q(o_00), .clk(clk), .clr(clr));
  Register #(.width(32)) register_10 (.D(i_00), .en(en), .Q(o_00), .clk(clk), .clr(clr));
  Register #(.width(32)) register_11 (.D(i_00), .en(en), .Q(o_00), .clk(clk), .clr(clr));
  Register #(.width(32)) register_12 (.D(i_00), .en(en), .Q(o_00), .clk(clk), .clr(clr));
  Register #(.width(32)) register_13 (.D(i_00), .en(en), .Q(o_00), .clk(clk), .clr(clr));
  Register #(.width(32)) register_14 (.D(i_00), .en(en), .Q(o_00), .clk(clk), .clr(clr));
  Register #(.width(32)) register_15 (.D(i_00), .en(en), .Q(o_00), .clk(clk), .clr(clr));
  Register #(.width(32)) register_16 (.D(i_00), .en(en), .Q(o_00), .clk(clk), .clr(clr));
  Register #(.width(32)) register_17 (.D(i_00), .en(en), .Q(o_00), .clk(clk), .clr(clr));
  Register #(.width(32)) register_18 (.D(i_00), .en(en), .Q(o_00), .clk(clk), .clr(clr));
  Register #(.width(32)) register_19 (.D(i_00), .en(en), .Q(o_00), .clk(clk), .clr(clr));
  Register #(.width(32)) register_20 (.D(i_00), .en(en), .Q(o_00), .clk(clk), .clr(clr));
  Register #(.width(32)) register_21 (.D(i_00), .en(en), .Q(o_00), .clk(clk), .clr(clr));
  Register #(.width(32)) register_22 (.D(i_00), .en(en), .Q(o_00), .clk(clk), .clr(clr));
  Register #(.width(32)) register_23 (.D(i_00), .en(en), .Q(o_00), .clk(clk), .clr(clr));
  Register #(.width(32)) register_24 (.D(i_00), .en(en), .Q(o_00), .clk(clk), .clr(clr));
  Register #(.width(32)) register_25 (.D(i_00), .en(en), .Q(o_00), .clk(clk), .clr(clr));
  Register #(.width(32)) register_26 (.D(i_00), .en(en), .Q(o_00), .clk(clk), .clr(clr));
  Register #(.width(32)) register_27 (.D(i_00), .en(en), .Q(o_00), .clk(clk), .clr(clr));
  Register #(.width(32)) register_28 (.D(i_00), .en(en), .Q(o_00), .clk(clk), .clr(clr));
  Register #(.width(32)) register_29 (.D(i_00), .en(en), .Q(o_00), .clk(clk), .clr(clr));
  Register #(.width(32)) register_30 (.D(i_00), .en(en), .Q(o_00), .clk(clk), .clr(clr));
  Register #(.width(32)) register_31 (.D(i_00), .en(en), .Q(o_00), .clk(clk), .clr(clr));
  Register #(.width(32)) register_32 (.D(i_00), .en(en), .Q(o_00), .clk(clk), .clr(clr));
endmodule
